# Fritzing sketch CircuitBose (saved by Fritzing 1.0.1rc)

parts:
  Part1 = Logic Level Converter
  Mod1 = Raspberry Pi 4B
  M1 = DC Motor [voltage_(max)=6V voltage_(min)=3V]
  M2 = DC Motor [voltage_(max)=6V voltage_(min)=3V]
  M3 = gear-motor
  M4 = gear-motor
  A1 = Dual VNH2SP30 Motor Driver [part_number=MD03A]
  A2 = Dual VNH2SP30 Motor Driver [part_number=MD03A]
  J1 = Basic Servo
  Mod2 = Arduino Sensor Shield v5.0
  DC1 = DC_DC_XL4016 [package=board_screw]
  M5 = RioRand LM2596
  LED1 = LED - 5mm [color="Red (633nm)" current=0.030A package="5 mm [THT]"]
  LED3 = smd LED [color="Red (633nm)" package="0805 [SMD]"]
  HC-SR04_Sensor_1 = HC-SR04 Ultrasonic Distance Sensor
  U1 = TRANSCHIPTC5747 [package=camera_sfv24r-2st_2]
  Part2 = InvenSense MPU6050
  BAT2 = Battery Holders [package=battcon_12mm_pth]
  RE1 = Hexadecimal Rotary Encoder [part_number=APEM-PT65-303 package=THT]
  RE2 = Hexadecimal Rotary Encoder [part_number=APEM-PT65-303 package=THT]
  LED4 = LED - 5mm [color="Red (633nm)" current=0.030A package="5 mm [THT]"]
  LED5 = smd LED [color="Red (633nm)" package="0805 [SMD]"]
  S1 = SWITCH-MOMENTARY-2 [package=tactile_switch_smd]
  S2 = SWITCH-MOMENTARY-2 [package=tactile_switch_smd]
  J2 = Basic Servo

nets:
  N1: Part1.TX2_LV, Mod1.GPIO23
  N2: Part1.RX2_LV, Mod1.GPIO3
  GND: Part1.GND, Mod1.GND, A1.Pin_7, A1.Pin_9, A1.pin_19, A2.Pin_7, A2.Pin_9, A2.pin_19, J1.gnd, Mod2.SD-GND, Mod2.SD-D11, Mod2.GND, Mod2.ParallelLCD-GND, Mod2.ParallelLCD-D11, Mod2.ParallelLCD-D10, DC1.IN-, M5.Pin_2, LED1.cathode, LED3.cathode, HC-SR04_Sensor_1.GND, Part2.GND, RE1.Output2Pin, RE2.Output2Pin, LED4.cathode, LED5.cathode, S2.1, J2.gnd
  N3: Part1.LV, Mod1.3V3
  N4: Part1.RX_LV, Mod1.GPIO2
  N5: Part1.TX_LV, Mod1.GPIO24
  N6: Part1.TX_HV, HC-SR04_Sensor_1.ECHO
  N7: Part1.RX_HV, A1.Pin_12, Part2.SDA, RE1.Output8pin, RE2.Output8pin
  VCC: Part1.HV, Mod1.5V, A1.Pin_8, A2.Pin_8, DC1.OUT+, HC-SR04_Sensor_1.VCC, Part2.VCC, RE1.Output1Pin, RE2.Output1Pin
  N8: Part1.RX2_HV, A1.Pin_4, Part2.SCL, RE1.Output4Pin, RE2.Output4Pin
  N9: Part1.TX2_HV, HC-SR04_Sensor_1.TRIG
  N10: Mod1.GPIO4, LED4.anode
  N11: Mod1.GPIO17, LED3.anode
  N12: Mod1.GPIO27, LED1.anode
  N13: Mod1.GPIO22, LED5.anode
  N14: Mod1.GPIO5, A2.Pin_3
  N15: Mod1.GPIO6, A2.Pin_2
  N16: Mod1.GPIO12, A2.Pin_12
  N17: Mod1.GPIO13, A2.Pin_4
  N18: Mod1.GPIO16, A2.Pin_13
  N19: Mod1.GPIO26, A2.Pin_14
  N20: Mod1.TR01_TAP, U1.SCLK
  N21: M1.pin_1, A1.Pin_21
  N22: M1.pin_2, A1.Pin_17
  N23: M2.pin_1, A1.Pin_20
  N24: M2.pin_2, A1.Pin_16
  N25: M3.pin_1, A2.Pin_21
  N26: M3.pin_2, A2.Pin_17
  N27: M4.pin_1, A2.Pin_20
  N28: M4.pin_2, A2.Pin_16
  N29: A1.Pin_6, DC1.IN+, M5.Pin_1, S1.2
  VCC_2: A2.Pin_6, J1.vcc, Mod2.VCC, Mod2.ParallelLCD-VCC, M5.Pin_3
  N30: J1.pulse, Mod2.SD-D13, Mod2.ParallelLCD-D13
  N31: Mod2.ParallelLCD-D12, J2.vcc
  N32: Mod2.ParallelLCD-D2, Mod2.SerialLCD-D2, J2.pulse
  N33: BAT2.+, S2.2
  N34: BAT2.-, S1.1
